# Fritzing sketch Projet SmartPatate BBoard (saved by Fritzing 0.9.3b)
breadboards: 1

parts:
  ArduinoUno = Arduino Uno (Rev3)
  R2 = Resistor [tolerance=±5% resistance=1M package=THT]
  R3 = Resistor [tolerance=±5% resistance=3.3k package=THT]
  C2 = Ceramic Capacitor [capacitance=0.1nF package="100 mil [THT, multilayer]"]
  R1 = Resistor [tolerance=±5% resistance=10k package=THT]
  L1 = Inductor [package="0805 [SMD]"]
  D1 = Diode [part_number=1N4548 package=diode-1n4001]
  C1 = Ceramic Capacitor [capacitance=10nF package="100 mil [THT, multilayer]"]

nets (from the schematic view):
  N1: ArduinoUno.A0, R2.Pin_0, C2.1, D1.C
  N2: ArduinoUno.D9_PWM, R1.Pin_1
  GND: ArduinoUno.GND, R2.Pin_1, R3.Pin_1, C2.0
  N3: R3.Pin_0, R1.Pin_0, L1.pin_1
  N4: L1.pin_0, D1.A, C1.0
