# Fritzing sketch Projet SmartPatate (saved by Fritzing 0.9.3b)

parts:
  ArduinoUno = Arduino Uno (Rev3)
  R1 = Resistor [tolerance=±5% resistance=10k package=THT]
  L1 = Inductor [package="400 mil [THT]"]
  C1 = Ceramic Capacitor [capacitance=10nF package="100 mil [THT, multilayer]"]
  D1 = Diode [part_number=1N4548 package=sma-diode_alt]
  R2 = Resistor [tolerance=±5% resistance=1M package=THT]
  R3 = Resistor [tolerance=±5% resistance=3.3k package=THT]
  C2 = Ceramic Capacitor [capacitance=0.1nF package="100 mil [THT, multilayer]"]

nets:
  N1: ArduinoUno.A0, D1.C, R2.Pin_0, R3.Pin_1, C2.1
  N2: ArduinoUno.D9_PWM, R1.Pin_1
  GND: ArduinoUno.GND, R2.Pin_1, C2.0
  N3: R1.Pin_0, L1.pin_1, R3.Pin_0
  N4: L1.pin_0, C1.0, D1.A
  Électrode: C1.1
